// Logisim project tennis.circ as structural Verilog: 13 circuits, main circuit main
module main (
);

  wire again, kinematiccontrollerbase_1_progagain, mode, modeout, winleft, winright;
  wire [3:0] binaryto3dig_1_hundreds, binaryto3dig_1_ones, binaryto3dig_1_tens, binaryto3dig_2_hundreds,
       binaryto3dig_2_ones, binaryto3dig_2_tens;
  wire [4:0] joystick_1_y, joystik, kinematiccontrollerbase_1_ballxout, kinematiccontrollerbase_1_ballyout,
       kinematiccontrollerbase_1_chip_id, kinematiccontrollerbase_1_leftbaryout,
       kinematiccontrollerbase_1_rightbaryout, process_1_rightbat, videosection_1_outballx,
       videosection_1_outbally, videosection_1_outchipid, videosection_1_outleftbary,
       videosection_1_outrightbary, videosection_2_outballx, videosection_2_outbally,
       videosection_2_outchipid, videosection_2_outleftbary, videosection_2_outrightbary,
       videosection_3_outballx, videosection_3_outbally, videosection_3_outchipid,
       videosection_3_outleftbary, videosection_3_outrightbary;
  wire [6:0] win_mode_1__1, win_mode_1__2, win_mode_1__3, win_mode_1__4, win_mode_1__5, win_mode_1__6,
       win_mode_1__7, win_mode_1__8, win_mode_1__9, win_mode_1__10, win_mode_1__11, win_mode_1__12,
       win_mode_1__13, win_mode_1__14, win_mode_1__15, win_mode_1__16, win_mode_1__17, win_mode_1__18,
       win_mode_1__19, win_mode_1__20, win_mode_1__21, win_mode_1__22, win_mode_1__23, win_mode_1__24,
       win_mode_1__25, win_mode_1__26, win_mode_1__27, win_mode_1__28, win_mode_1__29, win_mode_1__30,
       win_mode_1__31, win_mode_1__32;
  wire [7:0] kinematiccontrollerbase_1_scoreleft, kinematiccontrollerbase_1_scoreright,
       kinematiccontrollerbase_1_vxy, kinematiccontrollerbase_1_xprocess, kinematiccontrollerbase_1_yprocess;
  wire [31:0] videosection_1_col0, videosection_1_col1, videosection_1_col2, videosection_1_col3,
       videosection_1_col4, videosection_1_col5, videosection_1_col6, videosection_1_col7,
       videosection_2_col0, videosection_2_col1, videosection_2_col2, videosection_2_col3,
       videosection_2_col4, videosection_2_col5, videosection_2_col6, videosection_2_col7,
       videosection_3_col0, videosection_3_col1, videosection_3_col2, videosection_3_col3,
       videosection_3_col4, videosection_3_col5, videosection_3_col6, videosection_3_col7,
       videosection_4_col0, videosection_4_col1, videosection_4_col2, videosection_4_col3,
       videosection_4_col4, videosection_4_col5, videosection_4_col6, videosection_4_col7;

  Hex_Digit_Display hex_digit_display_1 (.value(binaryto3dig_1_tens));  // open: dp
  Hex_Digit_Display hex_digit_display_2 (.value(binaryto3dig_1_hundreds));  // open: dp
  Joystick #(.bits(5)) joystick_1 (.y(joystick_1_y));  // open: x
  CorrectJoystik correctjoystik_1 (.Joystik(joystick_1_y), .JoystikOut(joystik));
  Button u_AGAIN (.out(again));
  Button u_MODE (.out(mode));
  Process process_1 (
    .BallX(kinematiccontrollerbase_1_xprocess), .BallY(kinematiccontrollerbase_1_yprocess),
    .vxy(kinematiccontrollerbase_1_vxy), .rightbat(process_1_rightbat),
    .reset(kinematiccontrollerbase_1_progagain));
  Win_Mode win_mode_1 (
    .Mode(modeout), .WinLeft(winleft), .WinRight(winright), ._1(win_mode_1__1), ._9(win_mode_1__9),
    ._17(win_mode_1__17), ._25(win_mode_1__25), ._2(win_mode_1__2), ._10(win_mode_1__10),
    ._18(win_mode_1__18), ._26(win_mode_1__26), ._3(win_mode_1__3), ._11(win_mode_1__11),
    ._19(win_mode_1__19), ._27(win_mode_1__27), ._4(win_mode_1__4), ._12(win_mode_1__12),
    ._20(win_mode_1__20), ._28(win_mode_1__28), ._5(win_mode_1__5), ._13(win_mode_1__13),
    ._21(win_mode_1__21), ._29(win_mode_1__29), ._6(win_mode_1__6), ._14(win_mode_1__14),
    ._22(win_mode_1__22), ._30(win_mode_1__30), ._7(win_mode_1__7), ._15(win_mode_1__15),
    ._23(win_mode_1__23), ._31(win_mode_1__31), ._8(win_mode_1__8), ._16(win_mode_1__16),
    ._24(win_mode_1__24), ._32(win_mode_1__32));
  DotMatrix #(.matrixcols(32)) dotmatrix_1 (
    .col0(win_mode_1__1), .col1(win_mode_1__2), .col2(win_mode_1__3), .col3(win_mode_1__4),
    .col4(win_mode_1__5), .col5(win_mode_1__6), .col6(win_mode_1__7), .col7(win_mode_1__8),
    .col8(win_mode_1__9), .col9(win_mode_1__10), .col10(win_mode_1__11), .col11(win_mode_1__12),
    .col12(win_mode_1__13), .col13(win_mode_1__14), .col14(win_mode_1__15), .col15(win_mode_1__16),
    .col16(win_mode_1__17), .col17(win_mode_1__18), .col18(win_mode_1__19), .col19(win_mode_1__20),
    .col20(win_mode_1__21), .col21(win_mode_1__22), .col22(win_mode_1__23), .col23(win_mode_1__24),
    .col24(win_mode_1__25), .col25(win_mode_1__26), .col26(win_mode_1__27), .col27(win_mode_1__28),
    .col28(win_mode_1__29), .col29(win_mode_1__30), .col30(win_mode_1__31), .col31(win_mode_1__32));
  Hex_Digit_Display hex_digit_display_3 (.value(binaryto3dig_1_ones));  // open: dp
  Binaryto3Dig binaryto3dig_1 (
    .number(kinematiccontrollerbase_1_scoreleft), .hundreds(binaryto3dig_1_hundreds),
    .tens(binaryto3dig_1_tens), .ones(binaryto3dig_1_ones));
  DotMatrix #(.matrixcols(32), .matrixrows(32)) dotmatrix_2 (
    .col0(videosection_1_col0), .col1(videosection_1_col1), .col2(videosection_1_col2),
    .col3(videosection_1_col3), .col4(videosection_1_col4), .col5(videosection_1_col5),
    .col6(videosection_1_col6), .col7(videosection_1_col7), .col8(videosection_2_col0),
    .col9(videosection_2_col1), .col10(videosection_2_col2), .col11(videosection_2_col3),
    .col12(videosection_2_col4), .col13(videosection_2_col5), .col14(videosection_2_col6),
    .col15(videosection_2_col7), .col16(videosection_3_col0), .col17(videosection_3_col1),
    .col18(videosection_3_col2), .col19(videosection_3_col3), .col20(videosection_3_col4),
    .col21(videosection_3_col5), .col22(videosection_3_col6), .col23(videosection_3_col7),
    .col24(videosection_4_col0), .col25(videosection_4_col1), .col26(videosection_4_col2),
    .col27(videosection_4_col3), .col28(videosection_4_col4), .col29(videosection_4_col5),
    .col30(videosection_4_col6), .col31(videosection_4_col7));
  VideoSection videosection_1 (
    .BallX(kinematiccontrollerbase_1_ballxout), .BallY(kinematiccontrollerbase_1_ballyout),
    .LeftbarY(kinematiccontrollerbase_1_leftbaryout), .RightbarY(kinematiccontrollerbase_1_rightbaryout),
    .col1(videosection_1_col1), .col3(videosection_1_col3), .col5(videosection_1_col5),
    .col7(videosection_1_col7), .col0(videosection_1_col0), .col2(videosection_1_col2),
    .col4(videosection_1_col4), .col6(videosection_1_col6), .OutBallX(videosection_1_outballx),
    .OutBallY(videosection_1_outbally), .OutLeftbarY(videosection_1_outleftbary),
    .OutRightbarY(videosection_1_outrightbary), .ChipID(kinematiccontrollerbase_1_chip_id),
    .OutChipID(videosection_1_outchipid));
  KinematicControllerBase kinematiccontrollerbase_1 (
    .Reset(again), .RightbarY(process_1_rightbat), .ScoreLeft(kinematiccontrollerbase_1_scoreleft),
    .ScoreRight(kinematiccontrollerbase_1_scoreright), .BallXout(kinematiccontrollerbase_1_ballxout),
    .BallYout(kinematiccontrollerbase_1_ballyout), .Chip_ID(kinematiccontrollerbase_1_chip_id),
    .XProcess(kinematiccontrollerbase_1_xprocess), .YProcess(kinematiccontrollerbase_1_yprocess),
    .VXY(kinematiccontrollerbase_1_vxy), .progagain(kinematiccontrollerbase_1_progagain), .mode(mode),
    .modeout(modeout), .winleft(winleft), .winright(winright),
    .RightbarYOut(kinematiccontrollerbase_1_rightbaryout),
    .LeftbarYOut(kinematiccontrollerbase_1_leftbaryout), .LeftbarY(joystik));
  VideoSection videosection_2 (
    .BallX(videosection_1_outballx), .BallY(videosection_1_outbally), .LeftbarY(videosection_1_outleftbary),
    .RightbarY(videosection_1_outrightbary), .col1(videosection_2_col1), .col3(videosection_2_col3),
    .col5(videosection_2_col5), .col7(videosection_2_col7), .col0(videosection_2_col0),
    .col2(videosection_2_col2), .col4(videosection_2_col4), .col6(videosection_2_col6),
    .OutBallX(videosection_2_outballx), .OutBallY(videosection_2_outbally),
    .OutLeftbarY(videosection_2_outleftbary), .OutRightbarY(videosection_2_outrightbary),
    .ChipID(videosection_1_outchipid), .OutChipID(videosection_2_outchipid));
  VideoSection videosection_3 (
    .BallX(videosection_2_outballx), .BallY(videosection_2_outbally), .LeftbarY(videosection_2_outleftbary),
    .RightbarY(videosection_2_outrightbary), .col1(videosection_3_col1), .col3(videosection_3_col3),
    .col5(videosection_3_col5), .col7(videosection_3_col7), .col0(videosection_3_col0),
    .col2(videosection_3_col2), .col4(videosection_3_col4), .col6(videosection_3_col6),
    .OutBallX(videosection_3_outballx), .OutBallY(videosection_3_outbally),
    .OutLeftbarY(videosection_3_outleftbary), .OutRightbarY(videosection_3_outrightbary),
    .ChipID(videosection_2_outchipid), .OutChipID(videosection_3_outchipid));
  VideoSection videosection_4 (
    .BallX(videosection_3_outballx), .BallY(videosection_3_outbally), .LeftbarY(videosection_3_outleftbary),
    .RightbarY(videosection_3_outrightbary), .col1(videosection_4_col1), .col3(videosection_4_col3),
    .col5(videosection_4_col5), .col7(videosection_4_col7), .col0(videosection_4_col0),
    .col2(videosection_4_col2), .col4(videosection_4_col4), .col6(videosection_4_col6),
    .ChipID(videosection_3_outchipid));  // open: OutBallX, OutBallY, OutLeftbarY, OutRightbarY, OutChipID
  Hex_Digit_Display hex_digit_display_4 (.value(binaryto3dig_2_hundreds));  // open: dp
  Hex_Digit_Display hex_digit_display_5 (.value(binaryto3dig_2_tens));  // open: dp
  Hex_Digit_Display hex_digit_display_6 (.value(binaryto3dig_2_ones));  // open: dp
  Binaryto3Dig binaryto3dig_2 (
    .number(kinematiccontrollerbase_1_scoreright), .hundreds(binaryto3dig_2_hundreds),
    .tens(binaryto3dig_2_tens), .ones(binaryto3dig_2_ones));
endmodule

module VideoChip (
  input  [4:0] ChipID,
  input  [4:0] BallX,
  input  [4:0] BallY,
  input  [4:0] LeftbarY,
  input  [4:0] RightbarY,
  output [4:0] OutChipID,
  output [4:0] OutBallX,
  output [4:0] OutBallY,
  output [4:0] OutLeftbarY,
  output [4:0] OutRightbarY,
  output [31:0] Display
);

  wire ball, left, right;
  wire [31:0] and_1_out, and_2_out, and_3_out, bit_extender_1_out, bit_extender_2_out, bit_extender_3_out,
       shifter_1_out, shifter_2_out, shifter_3_out;

  Adder #(.width(5)) adder_1 (.a(ChipID), .b(5'b00001), .out(OutChipID));  // open: cin, cout
  Comparator #(.width(5)) comparator_1 (.a(ChipID), .b(BallX), .eq(ball));  // open: gt, lt
  // Probe on 32'h7
  assign bit_extender_1_out = {{31{left}}, left};  // Bit_Extender bit_extender_1
  assign bit_extender_2_out = {{31{right}}, right};  // Bit_Extender bit_extender_2
  assign bit_extender_3_out = {{31{ball}}, ball};  // Bit_Extender bit_extender_3
  Shifter #(.width(32)) shifter_1 (.in(32'h7), .\dist (LeftbarY), .out(shifter_1_out));
  Shifter #(.width(32)) shifter_2 (.in(32'h7), .\dist (RightbarY), .out(shifter_2_out));
  Shifter #(.width(32)) shifter_3 (.in(32'h1), .\dist (BallY), .out(shifter_3_out));
  assign and_1_out = shifter_1_out & bit_extender_1_out;  // AND_Gate and_1, 32 bits wide
  assign Display = and_1_out | and_2_out | and_3_out;  // OR_Gate or_1, 32 bits wide
  assign and_2_out = shifter_2_out & bit_extender_2_out;  // AND_Gate and_2, 32 bits wide
  assign and_3_out = shifter_3_out & bit_extender_3_out;  // AND_Gate and_3, 32 bits wide
  Comparator #(.width(5)) comparator_2 (.a(ChipID), .b(5'b00011), .eq(left));  // open: gt, lt
  // Probe on 5'b00011
  Comparator #(.width(5)) comparator_3 (.a(ChipID), .b(5'b11100), .eq(right));  // open: gt, lt
  // Probe on 5'b11100

  assign OutBallX = BallX;
  assign OutBallY = BallY;
  assign OutLeftbarY = LeftbarY;
  assign OutRightbarY = RightbarY;

  // Notes on the sheet:
  //   Ball Column?
  //   3 column?
  //   28 column?
endmodule

module VideoSection (
  input  [4:0] ChipID,
  input  [4:0] BallX,
  input  [4:0] BallY,
  input  [4:0] LeftbarY,
  input  [4:0] RightbarY,
  output [31:0] col1,
  output [31:0] col3,
  output [31:0] col5,
  output [31:0] col7,
  output [4:0] OutChipID,
  output [4:0] OutBallX,
  output [4:0] OutBallY,
  output [4:0] OutLeftbarY,
  output [4:0] OutRightbarY,
  output [31:0] col0,
  output [31:0] col2,
  output [31:0] col4,
  output [31:0] col6
);

  wire [4:0] videochip_1_outballx, videochip_1_outbally, videochip_1_outchipid, videochip_1_outleftbary,
       videochip_1_outrightbary, videochip_2_outballx, videochip_2_outbally, videochip_2_outchipid,
       videochip_2_outleftbary, videochip_2_outrightbary, videochip_3_outballx, videochip_3_outbally,
       videochip_3_outchipid, videochip_3_outleftbary, videochip_3_outrightbary, videochip_4_outballx,
       videochip_4_outbally, videochip_4_outchipid, videochip_4_outleftbary, videochip_4_outrightbary,
       videochip_5_outballx, videochip_5_outbally, videochip_5_outchipid, videochip_5_outleftbary,
       videochip_5_outrightbary, videochip_6_outballx, videochip_6_outbally, videochip_6_outchipid,
       videochip_6_outleftbary, videochip_6_outrightbary, videochip_7_outballx, videochip_7_outbally,
       videochip_7_outchipid, videochip_7_outleftbary, videochip_7_outrightbary;

  VideoChip videochip_1 (
    .ChipID(videochip_2_outchipid), .BallX(videochip_2_outballx), .BallY(videochip_2_outbally),
    .LeftbarY(videochip_2_outleftbary), .RightbarY(videochip_2_outrightbary),
    .OutChipID(videochip_1_outchipid), .OutBallX(videochip_1_outballx), .OutBallY(videochip_1_outbally),
    .OutLeftbarY(videochip_1_outleftbary), .OutRightbarY(videochip_1_outrightbary), .Display(col1));
  VideoChip videochip_2 (
    .ChipID(ChipID), .BallX(BallX), .BallY(BallY), .LeftbarY(LeftbarY), .RightbarY(RightbarY),
    .OutChipID(videochip_2_outchipid), .OutBallX(videochip_2_outballx), .OutBallY(videochip_2_outbally),
    .OutLeftbarY(videochip_2_outleftbary), .OutRightbarY(videochip_2_outrightbary), .Display(col0));
  VideoChip videochip_3 (
    .ChipID(videochip_1_outchipid), .BallX(videochip_1_outballx), .BallY(videochip_1_outbally),
    .LeftbarY(videochip_1_outleftbary), .RightbarY(videochip_1_outrightbary),
    .OutChipID(videochip_3_outchipid), .OutBallX(videochip_3_outballx), .OutBallY(videochip_3_outbally),
    .OutLeftbarY(videochip_3_outleftbary), .OutRightbarY(videochip_3_outrightbary), .Display(col2));
  VideoChip videochip_4 (
    .ChipID(videochip_5_outchipid), .BallX(videochip_5_outballx), .BallY(videochip_5_outbally),
    .LeftbarY(videochip_5_outleftbary), .RightbarY(videochip_5_outrightbary),
    .OutChipID(videochip_4_outchipid), .OutBallX(videochip_4_outballx), .OutBallY(videochip_4_outbally),
    .OutLeftbarY(videochip_4_outleftbary), .OutRightbarY(videochip_4_outrightbary), .Display(col4));
  VideoChip videochip_5 (
    .ChipID(videochip_3_outchipid), .BallX(videochip_3_outballx), .BallY(videochip_3_outbally),
    .LeftbarY(videochip_3_outleftbary), .RightbarY(videochip_3_outrightbary),
    .OutChipID(videochip_5_outchipid), .OutBallX(videochip_5_outballx), .OutBallY(videochip_5_outbally),
    .OutLeftbarY(videochip_5_outleftbary), .OutRightbarY(videochip_5_outrightbary), .Display(col3));
  VideoChip videochip_6 (
    .ChipID(videochip_4_outchipid), .BallX(videochip_4_outballx), .BallY(videochip_4_outbally),
    .LeftbarY(videochip_4_outleftbary), .RightbarY(videochip_4_outrightbary),
    .OutChipID(videochip_6_outchipid), .OutBallX(videochip_6_outballx), .OutBallY(videochip_6_outbally),
    .OutLeftbarY(videochip_6_outleftbary), .OutRightbarY(videochip_6_outrightbary), .Display(col5));
  VideoChip videochip_7 (
    .ChipID(videochip_6_outchipid), .BallX(videochip_6_outballx), .BallY(videochip_6_outbally),
    .LeftbarY(videochip_6_outleftbary), .RightbarY(videochip_6_outrightbary),
    .OutChipID(videochip_7_outchipid), .OutBallX(videochip_7_outballx), .OutBallY(videochip_7_outbally),
    .OutLeftbarY(videochip_7_outleftbary), .OutRightbarY(videochip_7_outrightbary), .Display(col6));
  VideoChip videochip_8 (
    .ChipID(videochip_7_outchipid), .BallX(videochip_7_outballx), .BallY(videochip_7_outbally),
    .LeftbarY(videochip_7_outleftbary), .RightbarY(videochip_7_outrightbary), .OutChipID(OutChipID),
    .OutBallX(OutBallX), .OutBallY(OutBallY), .OutLeftbarY(OutLeftbarY), .OutRightbarY(OutRightbarY),
    .Display(col7));
endmodule

module Reflect (
  input  [2:0] oldv,
  output [2:0] newv
);

  wire comparator_1_eq;
  wire [2:0] negator_1_out, not_1_out;

  Negator #(.width(3)) negator_1 (.in(oldv), .out(negator_1_out));
  assign not_1_out = ~oldv;  // NOT_Gate not_1, 3 bits wide
  Comparator #(.width(3)) comparator_1 (.a(oldv), .b(3'b100), .eq(comparator_1_eq));  // open: gt, lt
  Multiplexer #(.width(3)) multiplexer_1 (
    .in0(negator_1_out), .in1(not_1_out), .out(newv), .sel(comparator_1_eq));  // open: en

  // Notes on the sheet:
  //   Change speed of ball
  //   -(-4) = 3
endmodule

module Inrange (
  input  [4:0] Yball,
  input  [4:0] Ybat,
  output shareArrow
);

  wire comparator_1_eq, comparator_2_eq, comparator_3_eq;
  wire [4:0] adder_1_out, adder_2_out;

  Comparator #(.width(5)) comparator_1 (.a(Yball), .b(Ybat), .eq(comparator_1_eq));  // open: gt, lt
  Comparator #(.width(5)) comparator_2 (.a(Yball), .b(adder_1_out), .eq(comparator_2_eq));  // open: gt, lt
  Adder #(.width(5)) adder_1 (.a(Ybat), .b(5'b00001), .out(adder_1_out));  // open: cin, cout
  Comparator #(.width(5)) comparator_3 (.a(Yball), .b(adder_2_out), .eq(comparator_3_eq));  // open: gt, lt
  Adder #(.width(5)) adder_2 (.a(Ybat), .b(5'b00010), .out(adder_2_out));  // open: cin, cout
  or or_1 (shareArrow, comparator_1_eq, comparator_2_eq, comparator_3_eq);

  // Notes on the sheet:
  //   Is the ball in the same line with the bat?
endmodule

module KinematicControllerBase (
  input  Reset,
  input  mode,
  input  [4:0] LeftbarY,
  input  [4:0] RightbarY,
  output [4:0] Chip_ID,
  output modeout,
  output [4:0] BallXout,
  output winleft,
  output [4:0] BallYout,
  output winright,
  output [7:0] XProcess,
  output [7:0] YProcess,
  output [7:0] VXY,
  output progagain,
  output [4:0] LeftbarYOut,
  output [4:0] RightbarYOut,
  output [7:0] ScoreLeft,
  output [7:0] ScoreRight
);

  wire adder_3_cout, adder_4_cout, and_1_out, and_3_out, bat, carryX, carryY, Clock, clock_1_out,
       comparator_1_eq, comparator_2_eq, d_ff_2_q, inrange_1_sharearrow, inrange_2_sharearrow, left_bat,
       left_wall, max, or_1_out, or_2_out, or_3_out, or_5_out, or_7_out, or_10_out, Reset_t, ResetMode,
       resscor, right_bat, right_wall, rightWALL, vx_change, vy_change, wall, xor_1_out, xor_2_out;
  wire [2:0] multiplexer_6_out, multiplexer_7_out, multiplexer_8_out, multiplexer_9_out, multiplexer_10_out,
       randomspeed_1_speedout, reflect_1_newv, reflect_2_newv, vx_reg, vy_reg, Xregout, Yregout;
  wire [7:0] adder_1_out, adder_2_out, counter_1_q, counter_2_q, counter_3_q, counter_4_q, long_vx, long_vy,
       multiplexer_1_out, multiplexer_2_out, multiplexer_4_out, newXreg, newYreg;

  Counter #(.max('h11)) counter_1 (
    .count(right_wall), .Q(counter_1_q), .clk(Clock), .clr(resscor));  // open: load, D, carry
  Counter counter_2 (.count(right_wall), .Q(counter_2_q), .clk(Clock), .clr(Reset_t));  // open: load, D, carry
  Multiplexer #(.width(8)) multiplexer_1 (
    .in0(8'hd4), .in1(8'h28), .out(multiplexer_1_out), .sel(rightWALL));  // open: en
  // Probe on multiplexer_1_out
  and and_1 (and_1_out, ~vx_change, ~bat);  // AND_Gate
  or or_1 (or_1_out, and_1_out, ResetMode);
  // Probe on 8'h80
  Multiplexer #(.width(8)) multiplexer_2 (
    .in0(newYreg), .in1(8'h80), .out(multiplexer_2_out), .sel(ResetMode));  // open: en
  or or_2 (or_2_out, ~vy_change, ResetMode);  // OR_Gate
  Multiplexer #(.width(8)) multiplexer_3 (
    .in0(counter_1_q), .in1(counter_2_q), .out(ScoreLeft), .sel(modeout));  // open: en
  Counter #(.max('h11)) counter_3 (
    .count(left_wall), .Q(counter_3_q), .clk(Clock), .clr(resscor));  // open: load, D, carry
  Counter counter_4 (.count(left_wall), .Q(counter_4_q), .clk(Clock), .clr(Reset_t));  // open: load, D, carry
  // Probe on multiplexer_4_out
  Multiplexer #(.width(8)) multiplexer_4 (
    .in0(newXreg), .in1(multiplexer_1_out), .out(multiplexer_4_out), .sel(ResetMode));  // open: en
  // Probe on {BallYout, Yregout}
  Register #(.trigger("falling")) Yreg (
    .D(multiplexer_2_out), .en(or_2_out), .Q({BallYout, Yregout}), .clk(Clock));  // open: clr
  Comparator comparator_1 (.a(ScoreLeft), .b(8'hf), .eq(comparator_1_eq));  // open: gt, lt
  Comparator comparator_2 (.a(8'hf), .b(ScoreRight), .eq(comparator_2_eq));  // open: gt, lt
  Multiplexer #(.width(8)) multiplexer_5 (
    .in0(counter_3_q), .in1(counter_4_q), .out(ScoreRight), .sel(modeout));  // open: en
  // Probe on {BallXout, Xregout}
  Register #(.trigger("falling")) Xreg (
    .D(multiplexer_4_out), .en(or_1_out), .Q({BallXout, Xregout}), .clk(Clock));  // open: clr
  Counter #(.width(1), .max('h1)) counter_5 (
    .count(comparator_1_eq), .Q(winleft), .clk(Clock), .clr(Reset_t));  // open: load, D, carry
  Counter #(.width(1), .max('h1)) counter_6 (
    .count(comparator_2_eq), .Q(winright), .clk(Clock), .clr(Reset_t));  // open: load, D, carry
  or or_3 (or_3_out, winleft, winright);
  Register register_1 (.D({BallXout, Xregout}), .en(progagain), .Q(XProcess), .clk(Clock));  // open: clr
  and and_2 (max, ~modeout, or_3_out);  // AND_Gate
  or or_4 (resscor, max, Reset_t);
  Counter #(.width(1), .max('h1)) counter_7 (.Q(modeout), .clk(mode));  // open: load, D, count, carry, clr
  Register register_2 (.D({BallYout, Yregout}), .en(progagain), .Q(YProcess), .clk(Clock));  // open: clr
  Register register_3 (.D({2'b00, vy_reg, vx_reg}), .en(progagain), .Q(VXY), .clk(Clock));  // open: clr
  Adder adder_1 (.a({BallXout, Xregout}), .b(8'he4), .out(adder_1_out));  // open: cin, cout
  Adder adder_2 (.a({BallXout, Xregout}), .b(8'h1c), .out(adder_2_out));  // open: cin, cout
  and and_3 (and_3_out, ~modeout, or_5_out);  // AND_Gate
  or or_5 (or_5_out, right_wall, left_wall);
  Adder adder_3 (.a(adder_1_out), .b(long_vx), .cout(adder_3_cout));  // open: out, cin
  xor xor_1 (xor_1_out, adder_3_cout, vx_reg[2]);
  Inrange inrange_1 (.Yball(BallYout), .Ybat(LeftbarYOut), .shareArrow(inrange_1_sharearrow));
  Adder adder_4 (.a(adder_2_out), .b(long_vx), .cout(adder_4_cout));  // open: out, cin
  xor xor_2 (xor_2_out, adder_4_cout, vx_reg[2]);
  Inrange inrange_2 (.Yball(BallYout), .Ybat(RightbarYOut), .shareArrow(inrange_2_sharearrow));
  or or_6 (Reset_t, mode, Reset);
  Clock #(.highDuration(4), .lowDuration(4)) clock_1 (.out(clock_1_out));
  or or_7 (or_7_out, and_3_out, Reset_t);
  Register #(.width(1)) register_4 (.D(or_7_out), .Q(ResetMode), .clk(Clock));  // open: en, clr
  Reflect reflect_1 (.oldv(vy_reg), .newv(reflect_1_newv));
  and and_4 (left_bat, xor_1_out, inrange_1_sharearrow);
  and and_5 (right_bat, xor_2_out, inrange_2_sharearrow);
  and and_6 (Clock, clock_1_out, ~max);  // AND_Gate
  // Probe on 3'b001
  Multiplexer #(.width(3)) multiplexer_6 (
    .in0(vy_reg), .in1(randomspeed_1_speedout), .out(multiplexer_6_out), .sel(vy_change));  // open: en
  RandomSpeed randomspeed_1 (.Speed(reflect_1_newv), .SpeedOut(randomspeed_1_speedout));
  Bats bats_1 (
    .LeftbarY(LeftbarY), .LeftbarYOut(LeftbarYOut), .RightbarY(RightbarY), .RightbarYOut(RightbarYOut),
    .in_3(Clock), .XregIn({BallXout, Xregout}));
  Multiplexer #(.width(3)) multiplexer_7 (
    .in0(multiplexer_6_out), .in1(3'b001), .out(multiplexer_7_out), .sel(ResetMode));  // open: en
  xor xor_3 (wall, vx_reg[2], carryX);
  xor xor_4 (vy_change, vy_reg[2], carryY);
  or or_8 (bat, left_bat, right_bat);
  // Probe on multiplexer_9_out
  Multiplexer #(.width(3)) multiplexer_8 (
    .in0(vx_reg), .in1(reflect_2_newv), .out(multiplexer_8_out), .sel(vx_change));  // open: en
  Reflect reflect_2 (.oldv(vx_reg), .newv(reflect_2_newv));
  Multiplexer #(.width(3)) multiplexer_9 (
    .in0(3'b110), .in1(3'b010), .out(multiplexer_9_out), .sel(rightWALL));  // open: en
  assign long_vy = {{5{vy_reg[2]}}, vy_reg};  // Bit_Extender bit_extender_1
  Register #(.width(3)) VYreg (.D(multiplexer_7_out), .Q(vy_reg), .clk(Clock));  // open: en, clr
  or or_9 (vx_change, left_bat, right_bat, wall);
  Multiplexer #(.width(3)) multiplexer_10 (
    .in0(multiplexer_8_out), .in1(multiplexer_9_out), .out(multiplexer_10_out), .sel(ResetMode));  // open: en
  Adder adder_5 (.a(long_vy), .b({BallYout, Yregout}), .out(newYreg), .cout(carryY));  // open: cin
  or or_10 (or_10_out, rightWALL, left_bat, vy_change, left_wall);
  Register #(.width(3)) VXreg (.D(multiplexer_10_out), .Q(vx_reg), .clk(Clock));  // open: en, clr
  assign long_vx = {{5{vx_reg[2]}}, vx_reg};  // Bit_Extender bit_extender_2
  D_Flip_Flop d_ff_1 (.clk(Clock), .D(or_10_out), .Q(progagain));  // open: Qn, preset, en, reset
  and and_7 (right_wall, wall, ~vx_reg[2]);  // AND_Gate
  D_Flip_Flop d_ff_2 (.clk(Clock), .D(right_wall), .Q(d_ff_2_q));  // open: Qn, preset, en, reset
  and and_8 (left_wall, wall, vx_reg[2]);
  Adder adder_6 (.a(long_vx), .b({BallXout, Xregout}), .out(newXreg), .cout(carryX));  // open: cin
  and and_9 (rightWALL, ~modeout, d_ff_2_q);  // AND_Gate

  assign Chip_ID = {5{1'b0}};

  // Other names for the same wires on the sheet: BallX[4:0] = BallXout; Xregout[7:3] = BallXout;
  //   BallY[4:0] = BallYout; Yregout[7:3] = BallYout; changemode = mode; hit = progagain;
  //   LeftBarY_t[4:0] = LeftbarYOut; maxleft = winleft; maxright = winright; mode_t = modeout;
  //   RightBarY_t[4:0] = RightbarYOut; vx_sign = vx_reg[2]; vy_sign = vy_reg[2]

  // Notes on the sheet:
  //   Placement of Ball
  //   Scores + WIN/LOSE
  //   Reset + MODE + IN/OUT
  //   Out for robot
  //   Change VY
  //   Ball hit bat
  //   Change VX
  //   Coordinates robot
  //   Hit smth
endmodule

module Process (
  input  [7:0] BallX,
  input  [7:0] BallY,
  input  reset,
  input  [7:0] vxy,
  output [4:0] rightbat
);

  wire and_5_out, clock, comparator_1_eq, comparator_2_eq, comparator_3_eq, comparator_4_eq, data_nins, f3,
       f4, f5, go, mem, not_1_out, not_2_out, read_nwrite;
  wire [2:0] register_1_q;
  wire [7:0] addr, cdm_8_mark5_1_pc, cdm_8_mark5_1_r0, cdm_8_mark5_1_r2, cdm_8_mark5_1_sp,
       controlled_buffer_1_out, controlled_buffer_6_out, in, out;

  // Probe on cdm_8_mark5_1_r2
  // Probe on cdm_8_mark5_1_r2
  // Probe on cdm_8_mark5_1_r0
  // Probe on cdm_8_mark5_1_r0
  Clock clock_1 (.out(clock));
  // Probe on cdm_8_mark5_1_sp
  // Probe on cdm_8_mark5_1_pc
  CdM_8_mark5 cdm_8_mark5_1 (
    .clock(clock), .addr(addr), .mem_read(read_nwrite), .mem_cycle(mem), .data_inst(data_nins),
    .data_out(out), .data_in(in), .r0(cdm_8_mark5_1_r0), .r1(cdm_8_mark5_1_r0), .r2(cdm_8_mark5_1_r2),
    .r3(cdm_8_mark5_1_r2), .PC(cdm_8_mark5_1_pc), .SP(cdm_8_mark5_1_sp), .reset(reset));  // open: PS, IAck, IRQ, vec
  and and_1 (go, data_nins, ~f3, ~f4, ~f5);  // AND_Gate
  assign controlled_buffer_1_out = not_1_out ? out : 8'bz;  // Controlled_Buffer controlled_buffer_1
  not not_1 (not_1_out, read_nwrite);
  assign in = read_nwrite ? controlled_buffer_1_out : 8'bz;  // Controlled_Buffer controlled_buffer_2
  not not_2 (not_2_out, data_nins);
  Comparator comparator_1 (.a(addr), .b(8'hf3), .eq(comparator_1_eq));  // open: gt, lt
  and and_2 (f3, comparator_1_eq, read_nwrite, data_nins);
  Comparator comparator_2 (.a(addr), .b(8'hf4), .eq(comparator_2_eq));  // open: gt, lt
  and and_3 (f4, comparator_2_eq, read_nwrite, data_nins);
  Comparator comparator_3 (.a(addr), .b(8'hf5), .eq(comparator_3_eq));  // open: gt, lt
  and and_4 (f5, comparator_3_eq, read_nwrite, data_nins);
  Comparator comparator_4 (.a(addr), .b(8'hf3), .eq(comparator_4_eq));  // open: gt, lt
  and and_5 (and_5_out, comparator_4_eq, ~read_nwrite, data_nins);  // AND_Gate
  ROM rom_1 (.addr(addr), .data(controlled_buffer_1_out), .sel(not_2_out));
  RAM ram_1 (.addr(addr), .data(controlled_buffer_1_out), .sel(go), .clk(clock), .ld(read_nwrite));  // open: clr
  // Probe on BallX
  assign controlled_buffer_1_out = f3 ? BallX : 8'bz;  // Controlled_Buffer controlled_buffer_3
  // Probe on BallY
  assign controlled_buffer_1_out = f4 ? BallY : 8'bz;  // Controlled_Buffer controlled_buffer_4
  assign controlled_buffer_1_out = f5 ? vxy : 8'bz;  // Controlled_Buffer controlled_buffer_5
  assign controlled_buffer_6_out = and_5_out ? controlled_buffer_1_out : 8'bz;  // Controlled_Buffer controlled_buffer_6
  // Probe on {rightbat, register_1_q}
  Register register_1 (
    .D(controlled_buffer_6_out), .en(and_5_out), .Q({rightbat, register_1_q}), .clk(clock));  // open: clr
  // Probe on rightbat

  // Other names for the same wires on the sheet: BalX[7:0] = BallX

  // Notes on the sheet:
  //   contents of rom_1 (hex, n*v repeats v):
  //   d0 f5 b1 6 d0 4 41 d0 f3 b0 d1 e0 34 92 92 92 d1 7 46 d1 4 49 5 e0 1d 86 d3 7 4e d3 1 4b c1 35 f ed
  //   38 d3 3 90 7e e1 36 3 10 e3 31 d1 1 1c e3 36 d1 1 ee 42 d3 4 7e e1 42 10 e3 42 d1 1 7 c5 d2 f4 ba f
  //   e0 5b 5 e0 53 38 e3 51 84 ee 59 18 e3 58 ee 59 84 ee 6a 5 e0 66 38 e3 63 ee 64 84 ee 6a 18 e3 6a 84
  //   d3 f3 ac d4
endmodule

module CorrectJoystik (
  input  [4:0] Joystik,
  output [4:0] JoystikOut
);

  wire comparator_1_gt;
  wire [4:0] subtractor_1_out;

  // Probe on {5{1'b1}}
  Subtractor #(.width(5)) subtractor_1 (.a({5{1'b1}}), .b(Joystik), .out(subtractor_1_out));  // open: bin, bout
  // Probe on 5'b11101
  Multiplexer #(.width(5)) multiplexer_1 (
    .in0(subtractor_1_out), .in1(5'b11101), .out(JoystikOut), .sel(comparator_1_gt));  // open: en
  Comparator #(.width(5), .mode("unsigned")) comparator_1 (
    .a(subtractor_1_out), .b(5'b11101), .gt(comparator_1_gt));  // open: eq, lt

  // Notes on the sheet:
  //   Correct joystick
endmodule

module Binaryto3Dig (
  input  [7:0] number,
  output [3:0] hundreds,
  output [3:0] tens,
  output [3:0] ones
);

  wire [7:0] divider_1_out;
  wire [7:4] divider_1_rem, divider_2_out, divider_2_rem;

  // Probe on number
  Divider divider_1 (.a(number), .b(8'ha), .out(divider_1_out), .rem({divider_1_rem, ones}));  // open: upper
  Divider divider_2 (
    .a(divider_1_out), .b(8'ha), .out({divider_2_out, hundreds}), .rem({divider_2_rem, tens}));  // open: upper
  // Probe on ones
  // Probe on hundreds
  // Probe on tens

  // Notes on the sheet:
  //   Do the number from binary to decimal
endmodule

module RandomSpeed (
  input  [2:0] Speed,
  output [2:0] SpeedOut
);

  wire clock_1_out, comparator_1_eq, comparator_2_eq, or_1_out, xor_1_out;
  wire [1:0] multiplexer_1_out, random_1_out;
  wire [2:0] adder_1_out, bit_extender_1_out;

  Clock #(.highDuration(3), .lowDuration(3)) clock_1 (.out(clock_1_out));
  Random #(.width(2), .seed(12301029)) random_1 (.clk(clock_1_out), .out(random_1_out));  // open: next, clr
  Comparator #(.width(2)) comparator_1 (.a(random_1_out), .b(2'b10), .eq(comparator_1_eq));  // open: gt, lt
  assign bit_extender_1_out = {{1{multiplexer_1_out[1]}}, multiplexer_1_out};  // Bit_Extender bit_extender_1
  Multiplexer #(.width(2)) multiplexer_1 (
    .in0(random_1_out), .in1(2'b01), .out(multiplexer_1_out), .sel(comparator_1_eq));  // open: en
  // Probe on bit_extender_1_out
  xor xor_1 (xor_1_out, Speed[2], adder_1_out[2]);
  // Probe on Speed
  // Probe on adder_1_out
  Adder #(.width(3)) adder_1 (.a(bit_extender_1_out), .b(Speed), .out(adder_1_out));  // open: cin, cout
  Comparator #(.width(3)) comparator_2 (.a(adder_1_out), .b(3'b000), .eq(comparator_2_eq));  // open: gt, lt
  // Probe on SpeedOut
  Multiplexer #(.width(3)) multiplexer_2 (.in0(adder_1_out), .in1(Speed), .out(SpeedOut), .sel(or_1_out));  // open: en
  or or_1 (or_1_out, xor_1_out, comparator_2_eq);

  // Notes on the sheet:
  //   Diffusion of VY
endmodule

module CorrectRightBat (
  input  [4:0] RightBat,
  output [4:0] RightBatOut
);

  wire subtractor_1_bout;
  wire [4:0] subtractor_1_out;

  Subtractor #(.width(5)) subtractor_1 (
    .a(RightBat), .b(5'b00001), .out(subtractor_1_out), .bout(subtractor_1_bout));  // open: bin
  Multiplexer #(.width(5), .enable("false")) multiplexer_1 (
    .in0(subtractor_1_out), .in1(RightBat), .out(RightBatOut), .sel(subtractor_1_bout));

  // Notes on the sheet:
  //   Robot calculates the bottom pixel of the bat
  //   changes it to the middle pixel
endmodule

module Win_Mode (
  input  Mode,
  input  WinLeft,
  input  WinRight,
  output [6:0] _1,
  output [6:0] _2,
  output [6:0] _3,
  output [6:0] _4,
  output [6:0] _5,
  output [6:0] _6,
  output [6:0] _7,
  output [6:0] _8,
  output [6:0] _9,
  output [6:0] _10,
  output [6:0] _11,
  output [6:0] _12,
  output [6:0] _13,
  output [6:0] _14,
  output [6:0] _15,
  output [6:0] _16,
  output [6:0] _17,
  output [6:0] _18,
  output [6:0] _19,
  output [6:0] _20,
  output [6:0] _21,
  output [6:0] _22,
  output [6:0] _23,
  output [6:0] _24,
  output [6:0] _25,
  output [6:0] _26,
  output [6:0] _27,
  output [6:0] _28,
  output [6:0] _29,
  output [6:0] _30,
  output [6:0] _31,
  output [6:0] _32
);

  wire or_1_out;
  wire [1:0] des, multiplexer_21_out, multiplexer_26_out;

  Multiplexer #(.select(2), .width(7), .enable("false")) multiplexer_1 (
    .in0({7{1'b0}}), .in1({7{1'b0}}), .in2({7{1'b0}}), .in3({7{1'b0}}), .out(_1), .sel(des));
  Multiplexer #(.select(2), .width(7), .enable("false")) multiplexer_2 (
    .in0({7{1'b0}}), .in1(7'b0100100), .in2(7'b0100010), .in3({7{1'b0}}), .out(_9), .sel(des));
  Multiplexer #(.select(2), .width(7), .enable("false")) multiplexer_3 (
    .in0({7{1'b0}}), .in1(7'b0111110), .in2(7'b0111110), .in3(7'b0010100), .out(_17), .sel(des));
  Multiplexer #(.select(2), .width(7), .enable("false")) multiplexer_4 (
    .in0({7{1'b0}}), .in1(7'b0011110), .in2(7'b0111100), .in3({7{1'b0}}), .out(_25), .sel(des));
  Multiplexer #(.select(2), .width(7), .enable("false")) multiplexer_5 (
    .in0({7{1'b0}}), .in1(7'b0111110), .in2(7'b0111110), .in3(7'b0110100), .out(_2), .sel(des));
  Multiplexer #(.select(2), .width(7), .enable("false")) multiplexer_6 (
    .in0({7{1'b0}}), .in1(7'b0011000), .in2(7'b0011100), .in3({7{1'b0}}), .out(_10), .sel(des));
  Multiplexer #(.select(2), .width(7), .enable("false")) multiplexer_7 (
    .in0({7{1'b0}}), .in1(7'b0101010), .in2(7'b0101010), .in3(7'b0100010), .out(_18), .sel(des));
  Multiplexer #(.select(2), .width(7), .enable("false")) multiplexer_8 (
    .in0({7{1'b0}}), .in1({7{1'b0}}), .in2(7'b0000110), .in3({7{1'b0}}), .out(_26), .sel(des));
  Multiplexer #(.select(2), .width(7), .enable("false")) multiplexer_9 (
    .in0({7{1'b0}}), .in1(7'b0100000), .in2(7'b0100000), .in3(7'b0000010), .out(_3), .sel(des));
  Multiplexer #(.select(2), .width(7), .enable("false")) multiplexer_10 (
    .in0({7{1'b0}}), .in1({7{1'b0}}), .in2({7{1'b0}}), .in3(7'b0011100), .out(_11), .sel(des));
  Multiplexer #(.select(2), .width(7), .enable("false")) multiplexer_11 (
    .in0({7{1'b0}}), .in1(7'b0101010), .in2(7'b0101010), .in3(7'b0100010), .out(_19), .sel(des));
  Multiplexer #(.select(2), .width(7), .enable("false")) multiplexer_12 (
    .in0({7{1'b0}}), .in1(7'b0000010), .in2({7{1'b0}}), .in3(7'b0110100), .out(_27), .sel(des));
  Multiplexer #(.select(2), .width(7), .enable("false")) multiplexer_13 (
    .in0({7{1'b0}}), .in1(7'b0100000), .in2(7'b0100000), .in3(7'b0000010), .out(_4), .sel(des));
  Multiplexer #(.select(2), .width(7), .enable("false")) multiplexer_14 (
    .in0({7{1'b0}}), .in1(7'b0111110), .in2(7'b0111110), .in3(7'b0110100), .out(_5), .sel(des));
  Multiplexer #(.select(2), .width(7), .enable("false")) multiplexer_15 (
    .in0({7{1'b0}}), .in1(7'b0100010), .in2(7'b0101010), .in3(7'b0100010), .out(_13), .sel(des));
  Multiplexer #(.select(2), .width(7), .enable("false")) multiplexer_16 (
    .in0({7{1'b0}}), .in1(7'b0011100), .in2(7'b0111110), .in3(7'b0100010), .out(_12), .sel(des));
  Multiplexer #(.select(2), .width(7), .enable("false")) multiplexer_17 (
    .in0({7{1'b0}}), .in1(7'b0010100), .in2(7'b0100010), .in3(7'b0100010), .out(_20), .sel(des));
  Multiplexer #(.select(2), .width(7), .enable("false")) multiplexer_18 (
    .in0({7{1'b0}}), .in1({7{1'b0}}), .in2({7{1'b0}}), .in3(7'b0011100), .out(_21), .sel(des));
  Multiplexer #(.select(2), .width(7), .enable("false")) multiplexer_19 (
    .in0({7{1'b0}}), .in1(7'b0011100), .in2(7'b0011110), .in3(7'b0000010), .out(_28), .sel(des));
  Multiplexer #(.select(2), .width(7), .enable("false")) multiplexer_20 (
    .in0({7{1'b0}}), .in1(7'b0100000), .in2(7'b0100100), .in3(7'b0000010), .out(_29), .sel(des));
  Multiplexer #(.width(2)) multiplexer_21 (
    .in0(2'b01), .in1(2'b10), .out(multiplexer_21_out), .sel(WinLeft));  // open: en
  or or_1 (or_1_out, WinLeft, WinRight);
  Multiplexer #(.select(2), .width(7), .enable("false")) multiplexer_22 (
    .in0({7{1'b0}}), .in1({7{1'b0}}), .in2({7{1'b0}}), .in3({7{1'b0}}), .out(_6), .sel(des));
  Multiplexer #(.select(2), .width(7), .enable("false")) multiplexer_23 (
    .in0({7{1'b0}}), .in1(7'b0100010), .in2(7'b0101010), .in3(7'b0100010), .out(_14), .sel(des));
  Multiplexer #(.select(2), .width(7), .enable("false")) multiplexer_24 (
    .in0({7{1'b0}}), .in1(7'b0011110), .in2(7'b0000110), .in3({7{1'b0}}), .out(_22), .sel(des));
  Multiplexer #(.select(2), .width(7), .enable("false")) multiplexer_25 (
    .in0({7{1'b0}}), .in1(7'b0111110), .in2(7'b0100100), .in3(7'b0110100), .out(_30), .sel(des));
  Multiplexer #(.width(2)) multiplexer_26 (
    .in0(2'b00), .in1(multiplexer_21_out), .out(multiplexer_26_out), .sel(or_1_out));  // open: en
  Multiplexer #(.width(2)) multiplexer_27 (.in0(multiplexer_26_out), .in1(2'b11), .out(des), .sel(Mode));  // open: en
  Multiplexer #(.select(2), .width(7), .enable("false")) multiplexer_28 (
    .in0({7{1'b0}}), .in1(7'b0111110), .in2(7'b0011100), .in3({7{1'b0}}), .out(_7), .sel(des));
  Multiplexer #(.select(2), .width(7), .enable("false")) multiplexer_29 (
    .in0({7{1'b0}}), .in1(7'b0011100), .in2(7'b0000100), .in3(7'b0010100), .out(_15), .sel(des));
  Multiplexer #(.select(2), .width(7), .enable("false")) multiplexer_30 (
    .in0({7{1'b0}}), .in1(7'b0100100), .in2(7'b0011100), .in3({7{1'b0}}), .out(_23), .sel(des));
  Multiplexer #(.select(2), .width(7), .enable("false")) multiplexer_31 (
    .in0({7{1'b0}}), .in1({7{1'b0}}), .in2(7'b0011110), .in3({7{1'b0}}), .out(_31), .sel(des));
  Multiplexer #(.select(2), .width(7), .enable("false")) multiplexer_32 (
    .in0({7{1'b0}}), .in1(7'b0100100), .in2(7'b0100010), .in3({7{1'b0}}), .out(_8), .sel(des));
  Multiplexer #(.select(2), .width(7), .enable("false")) multiplexer_33 (
    .in0({7{1'b0}}), .in1({7{1'b0}}), .in2({7{1'b0}}), .in3(7'b0001000), .out(_16), .sel(des));
  Multiplexer #(.select(2), .width(7), .enable("false")) multiplexer_34 (
    .in0({7{1'b0}}), .in1(7'b0100100), .in2(7'b0100100), .in3({7{1'b0}}), .out(_24), .sel(des));
  Multiplexer #(.select(2), .width(7), .enable("false")) multiplexer_35 (
    .in0({7{1'b0}}), .in1({7{1'b0}}), .in2({7{1'b0}}), .in3({7{1'b0}}), .out(_32), .sel(des));

  // Notes on the sheet:
  //   Displaying the mode/result on the screen
  //   If mode 0:
  //   Not win - empty
  //   Winleft - ПОБЕДА
  //   Winright - ПРОВАЛ
  //   If mode 1, then infinity
  //   00
  //   10
  //   01
  //   11
endmodule

module Bats (
  input  [4:0] LeftbarY,
  input  [7:0] XregIn,
  input  in_3,
  input  [4:0] RightbarY,
  output [4:0] LeftbarYOut,
  output [4:0] RightbarYOut
);

  wire comparator_1_gt, comparator_2_gt, comparator_2_lt, comparator_3_gt, comparator_3_lt, comparator_4_lt;
  wire [4:0] adder_1_out, adder_2_out, correctrightbat_1_rightbatout, multiplexer_1_out, multiplexer_2_out,
       multiplexer_3_out, NextLeftBarY, NextRightBarY, subtractor_1_out, subtractor_2_out;

  CorrectRightBat correctrightbat_1 (.RightBat(RightbarY), .RightBatOut(correctrightbat_1_rightbatout));
  Multiplexer #(.width(5), .enable("false")) multiplexer_1 (
    .in0(correctrightbat_1_rightbatout), .in1(5'b11101), .out(multiplexer_1_out), .sel(comparator_1_gt));
  Comparator #(.width(5), .mode("unsigned")) comparator_1 (
    .a(correctrightbat_1_rightbatout), .b(5'b11101), .gt(comparator_1_gt));  // open: eq, lt
  Adder #(.width(5)) adder_1 (.a(LeftbarYOut), .b(5'b00001), .out(adder_1_out));  // open: cin, cout
  Multiplexer #(.width(5), .enable("false")) multiplexer_2 (
    .in0(LeftbarYOut), .in1(adder_1_out), .out(multiplexer_2_out), .sel(comparator_2_lt));
  Comparator #(.width(5), .mode("unsigned")) comparator_2 (
    .a(LeftbarYOut), .b(LeftbarY), .gt(comparator_2_gt), .lt(comparator_2_lt));  // open: eq
  Adder #(.width(5)) adder_2 (.a(RightbarYOut), .b(5'b00001), .out(adder_2_out));  // open: cin, cout
  Comparator #(.width(5), .mode("unsigned")) comparator_3 (
    .a(RightbarYOut), .b(multiplexer_1_out), .gt(comparator_3_gt), .lt(comparator_3_lt));  // open: eq
  Multiplexer #(.width(5), .enable("false")) multiplexer_3 (
    .in0(RightbarYOut), .in1(adder_2_out), .out(multiplexer_3_out), .sel(comparator_3_lt));
  Multiplexer #(.width(5), .enable("false")) multiplexer_4 (
    .in0(multiplexer_3_out), .in1(subtractor_1_out), .out(NextRightBarY), .sel(comparator_3_gt));
  Subtractor #(.width(5)) subtractor_1 (.a(RightbarYOut), .b(5'b00001), .out(subtractor_1_out));  // open: bin, bout
  // Probe on NextLeftBarY
  Multiplexer #(.width(5), .enable("false")) multiplexer_5 (
    .in0(multiplexer_2_out), .in1(subtractor_2_out), .out(NextLeftBarY), .sel(comparator_2_gt));
  Subtractor #(.width(5)) subtractor_2 (.a(LeftbarYOut), .b(5'b00001), .out(subtractor_2_out));  // open: bin, bout
  Register #(.width(5)) register_1 (.D(NextLeftBarY), .Q(LeftbarYOut), .clk(in_3));  // open: en, clr
  // Probe on LeftbarYOut
  Comparator #(.mode("unsigned")) comparator_4 (.a(XregIn), .b(8'h80), .lt(comparator_4_lt));  // open: gt, eq
  Register #(.width(5)) register_2 (
    .D(NextRightBarY), .en(comparator_4_lt), .Q(RightbarYOut), .clk(in_3));  // open: clr

  // Other names for the same wires on the sheet: Clock = in_3; LeftBarY_t[4:0] = LeftbarYOut;
  //   RightBarY_t[4:0] = RightbarYOut; Xreg[7:0] = XregIn

  // Notes on the sheet:
  //   Right Bat
  //   Smooth movements of bats with joystick correction
  //   Left Bat
endmodule
